# Fritzing sketch sketch (saved by Fritzing 0.9.3b)
breadboards: 1

parts:
  R1 = Resistor [tolerance=±20% resistance=470 package=THT]
  Part1 = Photon
  R2 = Resistor [tolerance=±20% resistance=470 package=THT]
  hc-sr1 = hc-sr04

nets:
  N1: R1.Pin_0, Part1.D5, R2.Pin_0
  GND: R1.Pin_1, Part1.GND, hc-sr1.GND
  VIN: Part1.VIN, hc-sr1.VCC
  N2: Part1.D4, hc-sr1.Trig
  N3: R2.Pin_1, hc-sr1.Echo
